// Logisim project 4BIT_2sComp.circ as structural Verilog: 1 circuit, main circuit main
module main (
  input  [3:0] in_1,
  output Y3,
  output Y2,
  output Y1,
  output Y0,
  output out_6
);

  wire not_1_out, not_2_out, not_3_out, not_4_out;

  not not_1 (not_1_out, in_1[3]);
  not not_2 (not_2_out, in_1[2]);
  not not_3 (not_3_out, in_1[1]);
  not not_4 (not_4_out, in_1[0]);
  _4BIT_INC_main main_1 (
    .A3(not_1_out), .A2(not_2_out), .A1(not_3_out), .A0(not_4_out), .INC(1'b1), .Y3(Y3), .CRY(out_6),
    .Y2(Y2), .Y1(Y1), .Y0(Y0));
endmodule
