// Logisim project 4BIT_Test.circ as structural Verilog: 1 circuit, main circuit main
module main (
  input  [3:0] in_1,
  input  in_2,
  output out_3
);

  wire [3:0] main_1_y0;

  _4BIT_INC_main main_1 (
    .A3(in_1[3]), .A2(in_1[2]), .A1(in_1[1]), .A0(in_1[0]), .INC(in_2), .Y3(main_1_y0[3]), .CRY(out_3),
    .Y2(main_1_y0[2]), .Y1(main_1_y0[1]), .Y0(main_1_y0[0]));
  Hex_Digit_Display hex_digit_display_1 (.value(main_1_y0));  // open: dp
endmodule
