// Logisim project 4BIT_INC.circ as structural Verilog: 1 circuit, main circuit main
module main (
  input  A3,
  input  A2,
  input  A1,
  input  A0,
  input  INC,
  output Y3,
  output CRY,
  output Y2,
  output Y1,
  output Y0
);

  wire main_2_cry, main_3_cry, main_4_cry;

  HA_1_main main_1 (.A(A3), .B(main_2_cry), .SUM(Y3), .CRY(CRY));
  HA_1_main main_2 (.A(A2), .B(main_3_cry), .SUM(Y2), .CRY(main_2_cry));
  HA_1_main main_3 (.A(A1), .B(main_4_cry), .SUM(Y1), .CRY(main_3_cry));
  HA_1_main main_4 (.A(A0), .B(INC), .SUM(Y0), .CRY(main_4_cry));
endmodule
