// Logisim project FA Built.circ as structural Verilog: 1 circuit, main circuit main
module main (
  input  A,
  input  B,
  input  C_in,
  output SUM,
  output CRY
);

  wire and_1_out, and_2_out, and_3_out, or_1_out, xor_1_out;

  xor xor_1 (xor_1_out, A, B);
  and and_1 (and_1_out, A, B);
  and and_2 (and_2_out, A, C_in);
  and and_3 (and_3_out, B, C_in);
  xor xor_2 (SUM, xor_1_out, C_in);
  or or_1 (or_1_out, and_1_out, and_2_out);
  or or_2 (CRY, or_1_out, and_3_out);

  // Notes on the sheet:
  //   1
  //   2
  //   74LS86
  //   LS7408
  //   1
  //   2
  //   4
  //   5
  //   LS7408
  //   10
  //   9
  //   LS7408
  //   3
  //   4
  //   5
  //   74LS86
  //   3
  //   74LS32
  //   1
  //   2
  //   6
  //   8
  //   6
  //   3
  //   4
  //   5
  //   74LS32
  //   6
endmodule
