// Logisim project HA_1.circ as structural Verilog: 1 circuit, main circuit main
module main (
  input  A,
  input  B,
  output SUM,
  output CRY
);

  wire and_1_out, and_2_out, not_1_out, not_2_out;

  not not_1 (not_1_out, A);
  not not_2 (not_2_out, B);
  and and_1 (and_1_out, not_1_out, B);
  and and_2 (and_2_out, A, not_2_out);
  and and_3 (CRY, A, B);
  or or_1 (SUM, and_1_out, and_2_out);
endmodule
