// Logisim project HA_Built.circ as structural Verilog: 1 circuit, main circuit main
module main (
  input  A,
  input  B,
  output SUM,
  output CRY
);

  wire not_1_out, not_2_out, or_1_out, or_2_out;

  not not_1 (not_1_out, A);
  not not_2 (not_2_out, B);
  or or_1 (or_1_out, A, B);
  or or_2 (or_2_out, not_1_out, not_2_out);
  and and_1 (SUM, or_1_out, or_2_out);
  and and_2 (CRY, A, B);

  // Notes on the sheet:
  //   1
  //   2
  //   1
  //   2
  //   74LS04
  //   3
  //   4
  //   74LS04
  //   3
  //   74LS32
  //   4
  //   6
  //   5
  //   74LS32
  //   4
  //   5
  //   1
  //   2
  //   74LS08
  //   6
  //   74LS08
  //   3
endmodule
