// Logisim project BUFFER_4.circ as structural Verilog: 1 circuit, main circuit main
module main (
  input  EN1,
  input  EN2,
  input  A0,
  input  A1,
  input  A2,
  input  A3,
  output Y0,
  output Y1,
  output Y2,
  output Y3
);

  wire and_1_out;

  and and_1 (and_1_out, EN1, EN2);
  assign Y0 = and_1_out ? A0 : 1'bz;  // Controlled_Buffer controlled_buffer_1
  assign Y1 = and_1_out ? A1 : 1'bz;  // Controlled_Buffer controlled_buffer_2
  assign Y2 = and_1_out ? A2 : 1'bz;  // Controlled_Buffer controlled_buffer_3
  assign Y3 = and_1_out ? A3 : 1'bz;  // Controlled_Buffer controlled_buffer_4
endmodule
