// Logisim project DECODER2_4.circ as structural Verilog: 1 circuit, main circuit main
module main (
  input  A0,
  input  A1,
  input  EN,
  output Y0,
  output Y1,
  output Y2,
  output Y3
);

  wire nand_1_out, nand_2_out, nand_3_out, nand_4_out, not_1_out, not_2_out, not_3_out, not_4_out;

  not not_1 (not_1_out, A0);
  not not_2 (not_2_out, A1);
  not not_3 (not_3_out, A1);
  not not_4 (not_4_out, A0);
  nand nand_1 (nand_1_out, not_1_out, not_2_out, EN);
  nand nand_2 (nand_2_out, A0, not_3_out, EN);
  nand nand_3 (nand_3_out, not_4_out, A1, EN);
  nand nand_4 (nand_4_out, A0, A1, EN);
  not not_5 (Y0, nand_1_out);
  not not_6 (Y1, nand_2_out);
  not not_7 (Y2, nand_3_out);
  not not_8 (Y3, nand_4_out);
endmodule
