// Logisim project DECODER4_16.circ as structural Verilog: 1 circuit, main circuit main
module main (
  input  A0,
  input  A1,
  input  A2,
  input  A3,
  input  EN,
  output Y0,
  output Y1,
  output Y2,
  output Y3,
  output Y4,
  output Y5,
  output Y6,
  output Y7,
  output Y8,
  output Y9,
  output Y10,
  output Y11,
  output Y12,
  output Y13,
  output Y14,
  output Y15
);

  wire main_1_y0, main_1_y1, main_1_y2, main_1_y3;

  DECODER2_4_main main_1 (.A0(A2), .A1(A3), .EN(EN), .Y0(main_1_y0), .Y1(main_1_y1), .Y2(main_1_y2), .Y3(main_1_y3));
  DECODER2_4_main main_2 (.A0(A0), .A1(A1), .EN(main_1_y0), .Y0(Y0), .Y1(Y1), .Y2(Y2), .Y3(Y3));
  DECODER2_4_main main_3 (.A0(A0), .A1(A1), .EN(main_1_y1), .Y0(Y4), .Y1(Y5), .Y2(Y6), .Y3(Y7));
  DECODER2_4_main main_4 (.A0(A0), .A1(A1), .EN(main_1_y2), .Y0(Y8), .Y1(Y9), .Y2(Y10), .Y3(Y11));
  DECODER2_4_main main_5 (.A0(A0), .A1(A1), .EN(main_1_y3), .Y0(Y12), .Y1(Y13), .Y2(Y14), .Y3(Y15));
endmodule
