// Logisim project DEC_1.circ as structural Verilog: 1 circuit, main circuit Dec_1
module Dec_1 (
  input  A0,
  input  EN,
  output Y0,
  output Y1
);

  wire nand_1_out, nand_2_out, not_1_out;

  not not_1 (not_1_out, A0);
  nand nand_1 (nand_1_out, A0, EN);
  nand nand_2 (nand_2_out, not_1_out, EN);
  not not_2 (Y1, nand_1_out);
  not not_3 (Y0, nand_2_out);
endmodule
