// Logisim project FA_1.circ as structural Verilog: 3 circuits, main circuit FA_Min
module FA_Min (
  input  A,
  input  B,
  input  C_In,
  output Sum,
  output C_Out
);

  wire nand_1_out, nand_2_out, nand_3_out;

  nand nand_1 (nand_1_out, B, C_In);
  nand nand_2 (nand_2_out, A, C_In);
  nand nand_3 (nand_3_out, A, B);
  xor xor_1 (Sum, A, B, C_In);
  nand nand_4 (C_Out, nand_1_out, nand_2_out, nand_3_out);
endmodule

module FA_INV_NAND (
  input  A,
  input  B,
  input  CIn,
  output Sum,
  output COut
);

  wire nand_1_out, nand_2_out, nand_3_out, nand_4_out, nand_5_out, nand_6_out, nand_7_out, not_1_out,
       not_2_out, not_3_out, not_4_out, not_5_out, not_6_out;

  not not_1 (not_1_out, A);
  not not_2 (not_2_out, B);
  not not_3 (not_3_out, A);
  not not_4 (not_4_out, CIn);
  not not_5 (not_5_out, B);
  not not_6 (not_6_out, CIn);
  nand nand_1 (nand_1_out, B, CIn);
  nand nand_2 (nand_2_out, A, CIn);
  nand nand_3 (nand_3_out, A, B);
  nand nand_4 (nand_4_out, not_1_out, not_2_out, CIn);
  nand nand_5 (nand_5_out, not_3_out, B, not_4_out);
  nand nand_6 (nand_6_out, A, not_5_out, not_6_out);
  nand nand_7 (nand_7_out, A, B, CIn);
  nand nand_8 (COut, nand_1_out, nand_2_out, nand_3_out);
  nand nand_9 (Sum, nand_4_out, nand_5_out, nand_6_out, nand_7_out);
endmodule

module FA_NAND_NAND (
  input  A,
  input  B,
  input  CIn,
  output Sum,
  output COut
);

  wire nand_1_out, nand_2_out, nand_3_out, nand_4_out, nand_5_out, nand_6_out, nand_7_out, nand_8_out,
       nand_9_out, nand_10_out, nand_11_out, nand_12_out, nand_13_out;

  nand nand_1 (nand_1_out, A, A);
  nand nand_2 (nand_2_out, B, B);
  nand nand_3 (nand_3_out, A, A);
  nand nand_4 (nand_4_out, CIn, CIn);
  nand nand_5 (nand_5_out, B, B);
  nand nand_6 (nand_6_out, CIn, CIn);
  nand nand_7 (nand_7_out, B, CIn);
  nand nand_8 (nand_8_out, A, CIn);
  nand nand_9 (nand_9_out, A, B);
  nand nand_10 (nand_10_out, nand_1_out, nand_2_out, CIn);
  nand nand_11 (nand_11_out, nand_3_out, B, nand_4_out);
  nand nand_12 (nand_12_out, A, nand_5_out, nand_6_out);
  nand nand_13 (nand_13_out, A, B, CIn);
  nand nand_14 (COut, nand_7_out, nand_8_out, nand_9_out);
  nand nand_15 (Sum, nand_10_out, nand_11_out, nand_12_out, nand_13_out);
endmodule
