// Logisim project FA_4.circ as structural Verilog: 1 circuit, main circuit main
module main (
  input  A3,
  input  A2,
  input  A1,
  input  A0,
  input  B3,
  input  B2,
  input  B1,
  input  B0,
  input  C_In,
  output S3,
  output C_Out,
  output S2,
  output S1,
  output S0
);

  wire fa_min_2_c_out, fa_min_3_c_out, fa_min_4_c_out;

  FA_Min fa_min_1 (.A(A3), .B(B3), .C_In(fa_min_2_c_out), .Sum(S3), .C_Out(C_Out));
  FA_Min fa_min_2 (.A(A2), .B(B2), .C_In(fa_min_3_c_out), .Sum(S2), .C_Out(fa_min_2_c_out));
  FA_Min fa_min_3 (.A(A1), .B(B1), .C_In(fa_min_4_c_out), .Sum(S1), .C_Out(fa_min_3_c_out));
  FA_Min fa_min_4 (.A(A0), .B(B0), .C_In(C_In), .Sum(S0), .C_Out(fa_min_4_c_out));
endmodule
