// Logisim project MUX_1.circ as structural Verilog: 1 circuit, main circuit main
module main (
  input  A,
  input  B,
  input  A_nB,
  output out_4
);

  wire nand_1_out, nand_2_out, not_1_out;

  not not_1 (not_1_out, A_nB);
  nand nand_1 (nand_1_out, A, A_nB);
  nand nand_2 (nand_2_out, B, not_1_out);
  nand nand_3 (out_4, nand_1_out, nand_2_out);
endmodule
