// Logisim project MUX_4.circ as structural Verilog: 1 circuit, main circuit main
module main (
  input  A3,
  input  A2,
  input  A1,
  input  A0,
  input  B3,
  input  B2,
  input  B1,
  input  B0,
  input  A_nB,
  output Y3,
  output Y2,
  output Y1,
  output Y0
);

  MUX_1_main main_1 (.A(A3), .B(B3), .A_nB(A_nB), .out_4(Y3));
  MUX_1_main main_2 (.A(A2), .B(B2), .A_nB(A_nB), .out_4(Y2));
  MUX_1_main main_3 (.A(A1), .B(B1), .A_nB(A_nB), .out_4(Y1));
  MUX_1_main main_4 (.A(A0), .B(B0), .A_nB(A_nB), .out_4(Y0));
endmodule
