// Logisim project MUX_4Test.circ as structural Verilog: 1 circuit, main circuit main
module main (
  input  [3:0] in_1,
  input  [3:0] in_2,
  input  in_3
);

  wire [3:0] main_1_y0;

  MUX_4_main main_1 (
    .A3(in_1[3]), .A2(in_1[2]), .A1(in_1[1]), .A0(in_1[0]), .B3(in_2[3]), .B2(in_2[2]), .B1(in_2[1]),
    .B0(in_2[0]), .A_nB(in_3), .Y3(main_1_y0[3]), .Y2(main_1_y0[2]), .Y1(main_1_y0[1]), .Y0(main_1_y0[0]));
  Hex_Digit_Display hex_digit_display_1 (.value(main_1_y0));  // open: dp
endmodule
