// Logisim project ADD_AND.circ as structural Verilog: 1 circuit, main circuit main
module main (
  input  A3,
  input  A2,
  input  A1,
  input  A0,
  input  B3,
  input  B2,
  input  B1,
  input  B0,
  input  AND_nADD,
  input  C_in,
  input  nPASS,
  output Y3,
  output Y2,
  output Y1,
  output Y0,
  output C_Out
);

  wire main_1_c_out, main_2_y0, main_2_y1, main_2_y2, main_2_y3;
  wire [3:0] and_4_out, main_1_s0;

  and and_1 (and_4_out[3], B3, A3);
  and and_2 (and_4_out[2], B2, A2);
  and and_3 (and_4_out[1], B1, A1);
  and and_4 (and_4_out[0], B0, A0);
  FA_4_main main_1 (
    .A3(A3), .A2(A2), .A1(A1), .A0(A0), .B3(B3), .B2(B2), .B1(B1), .B0(B0), .C_In(C_in), .S3(main_1_s0[3]),
    .C_Out(main_1_c_out), .S2(main_1_s0[2]), .S1(main_1_s0[1]), .S0(main_1_s0[0]));
  MUX_4_main main_2 (
    .A3(and_4_out[3]), .A2(and_4_out[2]), .A1(and_4_out[1]), .A0(and_4_out[0]), .B3(main_1_s0[3]),
    .B2(main_1_s0[2]), .B1(main_1_s0[1]), .B0(main_1_s0[0]), .A_nB(AND_nADD), .Y3(main_2_y3), .Y2(main_2_y2),
    .Y1(main_2_y1), .Y0(main_2_y0));
  MUX_4_main main_3 (
    .A3(main_2_y3), .A2(main_2_y2), .A1(main_2_y1), .A0(main_2_y0), .B3(A3), .B2(A2), .B1(A1), .B0(A0),
    .A_nB(nPASS), .Y3(Y3), .Y2(Y2), .Y1(Y1), .Y0(Y0));
  and and_5 (C_Out, main_1_c_out, nPASS);
endmodule
