// Logisim project ALU.circ as structural Verilog: 1 circuit, main circuit main
module main (
  input  A3,
  input  A2,
  input  A1,
  input  A0,
  input  B3,
  input  B2,
  input  B1,
  input  B0,
  input  C_in,
  input  Logic__nArith,
  input  nInvert,
  input  nA_Only,
  output Y3,
  output Y2,
  output Y1,
  output Y0,
  output C_Out
);

  wire main_1_y0, main_1_y1, main_1_y2, main_1_y3, not_1_out;

  not not_1 (not_1_out, nInvert);
  NOT_NEG_main main_1 (
    .A3(A3), .A2(A2), .A1(A1), .A0(A0), .nPass(not_1_out), .NOT_nNEG(Logic__nArith), .Y3(main_1_y3),
    .Y2(main_1_y2), .Y1(main_1_y1), .Y0(main_1_y0));  // open: C_Out
  ADD_AND_main main_2 (
    .A3(main_1_y3), .A2(main_1_y2), .A1(main_1_y1), .A0(main_1_y0), .B3(B3), .B2(B2), .B1(B1), .B0(B0),
    .AND_nADD(Logic__nArith), .C_in(C_in), .nPASS(nA_Only), .Y3(Y3), .Y2(Y2), .Y1(Y1), .Y0(Y0), .C_Out(C_Out));
endmodule
