// Logisim project Flip_Flop.circ as structural Verilog: 1 circuit, main circuit main
module main (
  input  CLK,
  input  D,
  input  CLR,
  input  PRE,
  input  EN,
  input  J,
  input  CLK_2,
  input  K,
  input  CLR_2,
  input  PRE_2,
  input  EN_2,
  output out_12,
  output out_13,
  output out_14,
  output out_15
);

  D_Flip_Flop d_ff_1 (.clk(CLK), .D(D), .Q(out_12), .Qn(out_13), .preset(PRE), .en(EN), .reset(CLR));
  J_K_Flip_Flop j_k_ff_1 (.J(J), .clk(CLK_2), .K(K), .Q(out_14), .Qn(out_15), .preset(PRE_2), .en(EN_2), .reset(CLR_2));
endmodule
