// Logisim project NOT_NEG.circ as structural Verilog: 1 circuit, main circuit main
module main (
  input  A3,
  input  A2,
  input  A1,
  input  A0,
  input  nPass,
  input  NOT_nNEG,
  output Y3,
  output Y2,
  output Y1,
  output Y0,
  output C_Out
);

  wire and_1_out, not_1_out, xor_1_out, xor_2_out, xor_3_out, xor_4_out;

  not not_1 (not_1_out, NOT_nNEG);
  xor xor_1 (xor_1_out, nPass, A3);
  xor xor_2 (xor_2_out, nPass, A2);
  xor xor_3 (xor_3_out, nPass, A1);
  xor xor_4 (xor_4_out, nPass, A0);
  and and_1 (and_1_out, nPass, not_1_out);
  _4BIT_INC_main main_1 (
    .A3(xor_1_out), .A2(xor_2_out), .A1(xor_3_out), .A0(xor_4_out), .INC(and_1_out), .Y3(Y3), .CRY(C_Out),
    .Y2(Y2), .Y1(Y1), .Y0(Y0));
endmodule
