// Logisim project HW try.circ as structural Verilog: 1 circuit, main circuit main
module main (
  input  in_1,
  input  in_2,
  input  in_3,
  input  in_4,
  output out_5,
  output out_6,
  output out_7,
  output out_8,
  output out_9
);

  wire n7402_1_p3, n7402_1_p4, n7404_1_p4, n7404_1_p6, n7404_1_p9, n7408_1_p1, n7408_1_p8, n7408_2_p1,
       n7408_2_p6, n7474_1_p2;

  // _7402 7402_1: pin names not known; wires that end beside it: 1'b1, out_5, n7402_1_p3, n7402_1_p4
  // _7404 7404_1: pin names not known; wires that end beside it: 1'b0, 1'b1, n7402_1_p4, n7404_1_p4, out_7, n7404_1_p6, n7402_1_p4, out_9, n7404_1_p9
  // _7408 7408_1: pin names not known; wires that end beside it: n7408_1_p1, 1'b0, 1'b1, n7404_1_p4, n7404_1_p6, in_3, n7402_1_p3, n7408_1_p8, out_6, in_3, n7402_1_p3
  // _7408 7408_2: pin names not known; wires that end beside it: n7408_2_p1, 1'b0, 1'b1, n7404_1_p9, in_4, n7408_2_p6, in_4, n7402_1_p4, n7402_1_p4
  // _7474 7474_1: pin names not known; wires that end beside it: n7408_1_p1, n7474_1_p2, out_8, 1'b0, 1'b1, in_1, in_1, n7408_1_p8, n7408_2_p1, in_2, in_2, n7402_1_p3, out_7
  // _7474 7474_2: pin names not known; wires that end beside it: 1'b0, 1'b1, in_1, in_1, n7408_2_p6, n7474_1_p2, in_2, in_2, n7402_1_p4, out_9, 1'b0
endmodule
