// Logisim project Mealy.circ as structural Verilog: 1 circuit, main circuit main
module main (
  input  P1_Score,
  input  CLK,
  input  P2_Score,
  input  CLR,
  output P1_Up_1,
  output P1_Wins,
  output P2_Wins,
  output P2_Up_by_One,
  output Tied
);

  wire and_1_out, and_2_out, and_3_out, and_4_out, d_ff_1_q, d_ff_2_q, not_1_out, not_2_out, not_3_out,
       not_4_out;

  and and_1 (and_1_out, P1_Score, not_1_out);
  not not_1 (not_1_out, d_ff_2_q);
  not not_2 (not_2_out, d_ff_1_q);
  and and_2 (and_2_out, not_2_out, P2_Score);
  D_Flip_Flop d_ff_1 (.clk(CLK), .D(and_1_out), .Q(d_ff_1_q), .en(1'b1), .reset(CLR));  // open: Qn, preset
  D_Flip_Flop d_ff_2 (.clk(CLK), .D(and_2_out), .Q(d_ff_2_q), .en(1'b1), .reset(CLR));  // open: Qn, preset
  not not_3 (not_3_out, P2_Wins);
  not not_4 (not_4_out, P1_Wins);
  and and_3 (and_3_out, d_ff_1_q, P1_Score);
  and and_4 (and_4_out, d_ff_2_q, P2_Score);
  and and_5 (P2_Up_by_One, not_3_out, d_ff_2_q);
  and and_6 (P1_Up_1, d_ff_1_q, not_4_out);
  D_Flip_Flop d_ff_3 (.clk(CLK), .D(and_3_out), .Q(P1_Wins), .en(1'b1));  // open: Qn, preset, reset
  D_Flip_Flop d_ff_4 (.clk(CLK), .D(and_4_out), .Q(P2_Wins), .en(1'b1));  // open: Qn, preset, reset
  nor nor_1 (Tied, d_ff_2_q, d_ff_1_q);
endmodule
