// Logisim project Brainless Micro_ ALU.circ as structural Verilog: 9 circuits, main circuit ACC + ALU
module ACC___ALU (
  input  [3:0] in_1,
  input  Logic_nArith,
  input  nInvert,
  input  nA_Only,
  input  Load_ACC,
  input  ACC_to_Data_Bus,
  input  Clock,
  input  Reset
);

  wire [3:0] main_1_y0, register_1_q;

  ALU_main main_1 (
    .A3(in_1[3]), .A2(in_1[2]), .A1(in_1[1]), .A0(in_1[0]), .B3(register_1_q[3]), .B2(register_1_q[2]),
    .B1(register_1_q[1]), .B0(register_1_q[0]), .C_in(1'b0), .Logic__nArith(Logic_nArith), .nInvert(nInvert),
    .nA_Only(nA_Only), .Y3(main_1_y0[3]), .Y2(main_1_y0[2]), .Y1(main_1_y0[1]), .Y0(main_1_y0[0]));  // open: C_Out
  Hex_Digit_Display hex_digit_display_1 (.value(main_1_y0));  // open: dp
  Hex_Digit_Display hex_digit_display_2 (.value(register_1_q));  // open: dp
  Register #(.width(4)) register_1 (.D(main_1_y0), .en(Load_ACC), .Q(register_1_q), .clk(Clock), .clr(Reset));
  Hex_Digit_Display hex_digit_display_3 (.value(in_1));  // open: dp
  assign in_1 = ACC_to_Data_Bus ? register_1_q : 4'bz;  // Controlled_Buffer controlled_buffer_1

  // Notes on the sheet:
  //   Data Bus
  //   Accumulator Register
  //   Feedback Path
endmodule

module Addressing_Logic (
  input  [3:0] Address_Bus
);

  wire [7:0] main_1_y0;

  Hex_Digit_Display hex_digit_display_1 (.value(Address_Bus));  // open: dp
  DECODER4_16_main main_1 (
    .A0(Address_Bus[0]), .A1(Address_Bus[1]), .A2(Address_Bus[2]), .A3(Address_Bus[3]), .EN(1'b1),
    .Y0(main_1_y0[0]), .Y1(main_1_y0[1]), .Y2(main_1_y0[2]), .Y3(main_1_y0[3]), .Y4(main_1_y0[4]),
    .Y5(main_1_y0[5]), .Y6(main_1_y0[6]), .Y7(main_1_y0[7]));  // open: Y8, Y9, Y10, Y11, Y12, Y13, Y14, Y15

  // Notes on the sheet:
  //   Memory Select Lines
endmodule

module _4_Bit_ROM (
  input  [3:0] in_1,
  input  Read,
  input  Memory_Select
);

  wire and_1_out;
  wire [3:0] controlled_buffer_1_out;

  and and_1 (and_1_out, Read, Memory_Select);
  assign controlled_buffer_1_out = and_1_out ? in_1 : 4'bz;  // Controlled_Buffer controlled_buffer_1

  // Notes on the sheet:
  //   Data Bus
endmodule

module _4_Bit_Output (
  input  [3:0] Data_Bus,
  input  Memory_Select,
  input  Write,
  input  Clock,
  input  Reset
);

  wire and_1_out;
  wire [3:0] register_1_q;

  and and_1 (and_1_out, Memory_Select, Write);
  Register #(.width(4)) register_1 (.D(Data_Bus), .en(and_1_out), .Q(register_1_q), .clk(Clock), .clr(Reset));
  Hex_Digit_Display hex_digit_display_1 (.value(register_1_q));  // open: dp
endmodule

module _4_Bit_RAM (
  input  [3:0] Data_Bus,
  input  Memory_Select,
  input  Write,
  input  Read,
  input  Clock,
  input  Reset
);

  wire and_1_out, and_2_out;
  wire [3:0] controlled_buffer_1_out, register_1_q;

  and and_1 (and_1_out, Memory_Select, Write);
  and and_2 (and_2_out, Memory_Select, Read);
  Register #(.width(4)) register_1 (.D(Data_Bus), .en(and_1_out), .Q(register_1_q), .clk(Clock), .clr(Reset));
  assign controlled_buffer_1_out = and_2_out ? register_1_q : 4'bz;  // Controlled_Buffer controlled_buffer_1
  Hex_Digit_Display hex_digit_display_1 (.value(controlled_buffer_1_out));  // open: dp
endmodule

module Brainless_Micro (
  input  [3:0] Address_Bus,
  input  [3:0] in_2,
  input  [3:0] in_3,
  input  Logic_nArith,
  input  nInvert,
  input  [3:0] in_6,
  input  [3:0] in_7,
  input  nA_Only,
  input  Load_ACC,
  input  [3:0] in_10,
  input  [3:0] in_11,
  input  ACC_to_Data_Bus,
  input  Write,
  input  [3:0] in_14,
  input  [3:0] in_15,
  input  Read,
  input  Clock,
  input  Reset
);

  wire and_1_out, and_2_out, and_3_out, and_4_out, and_5_out, and_6_out, and_7_out, and_8_out, and_9_out,
       and_10_out, and_11_out, main_2_y14, main_2_y15;
  wire [3:0] controlled_buffer_1_out, main_1_y0, register_1_q, register_2_q, register_3_q;
  wire [7:0] main_2_y0;

  Hex_Digit_Display hex_digit_display_1 (.value(main_1_y0));  // open: dp
  ALU_main main_1 (
    .A3(controlled_buffer_1_out[3]), .A2(controlled_buffer_1_out[2]), .A1(controlled_buffer_1_out[1]),
    .A0(controlled_buffer_1_out[0]), .B3(register_1_q[3]), .B2(register_1_q[2]), .B1(register_1_q[1]),
    .B0(register_1_q[0]), .C_in(1'b0), .Logic__nArith(Logic_nArith), .nInvert(nInvert), .nA_Only(nA_Only),
    .Y3(main_1_y0[3]), .Y2(main_1_y0[2]), .Y1(main_1_y0[1]), .Y0(main_1_y0[0]));  // open: C_Out
  Register #(.width(4)) register_1 (.D(main_1_y0), .en(Load_ACC), .Q(register_1_q), .clk(Clock), .clr(Reset));
  Hex_Digit_Display hex_digit_display_2 (.value(register_1_q));  // open: dp
  assign controlled_buffer_1_out = ACC_to_Data_Bus ? register_1_q : 4'bz;  // Controlled_Buffer controlled_buffer_1
  Hex_Digit_Display hex_digit_display_3 (.value(Address_Bus));  // open: dp
  and and_1 (and_1_out, main_2_y14, Write);
  and and_2 (and_2_out, main_2_y15, Write);
  and and_3 (and_3_out, main_2_y15, Read);
  Hex_Digit_Display hex_digit_display_4 (.value(register_2_q));  // open: dp
  Register #(.width(4)) register_2 (
    .D(controlled_buffer_1_out), .en(and_1_out), .Q(register_2_q), .clk(Clock), .clr(Reset));
  Register #(.width(4)) register_3 (
    .D(controlled_buffer_1_out), .en(and_2_out), .Q(register_3_q), .clk(Clock), .clr(Reset));
  DECODER4_16_main main_2 (
    .A0(Address_Bus[0]), .A1(Address_Bus[1]), .A2(Address_Bus[2]), .A3(Address_Bus[3]), .EN(1'b1),
    .Y0(main_2_y0[0]), .Y1(main_2_y0[1]), .Y2(main_2_y0[2]), .Y3(main_2_y0[3]), .Y4(main_2_y0[4]),
    .Y5(main_2_y0[5]), .Y6(main_2_y0[6]), .Y7(main_2_y0[7]), .Y14(main_2_y14), .Y15(main_2_y15));  // open: Y8, Y9, Y10, Y11, Y12, Y13
  assign controlled_buffer_1_out = and_3_out ? register_3_q : 4'bz;  // Controlled_Buffer controlled_buffer_2
  assign controlled_buffer_1_out = and_4_out ? in_2 : 4'bz;  // Controlled_Buffer controlled_buffer_3
  and and_4 (and_4_out, Read, main_2_y0[0]);
  assign controlled_buffer_1_out = and_5_out ? in_6 : 4'bz;  // Controlled_Buffer controlled_buffer_4
  and and_5 (and_5_out, Read, main_2_y0[1]);
  assign controlled_buffer_1_out = and_6_out ? in_10 : 4'bz;  // Controlled_Buffer controlled_buffer_5
  and and_6 (and_6_out, Read, main_2_y0[2]);
  assign controlled_buffer_1_out = and_7_out ? in_14 : 4'bz;  // Controlled_Buffer controlled_buffer_6
  and and_7 (and_7_out, Read, main_2_y0[3]);
  Hex_Digit_Display hex_digit_display_5 (.value(controlled_buffer_1_out));  // open: dp
  and and_8 (and_8_out, Read, main_2_y0[4]);
  and and_9 (and_9_out, Read, main_2_y0[5]);
  and and_10 (and_10_out, Read, main_2_y0[6]);
  and and_11 (and_11_out, Read, main_2_y0[7]);
  assign controlled_buffer_1_out = and_8_out ? in_3 : 4'bz;  // Controlled_Buffer controlled_buffer_7
  assign controlled_buffer_1_out = and_9_out ? in_7 : 4'bz;  // Controlled_Buffer controlled_buffer_8
  assign controlled_buffer_1_out = and_10_out ? in_11 : 4'bz;  // Controlled_Buffer controlled_buffer_9
  assign controlled_buffer_1_out = and_11_out ? in_15 : 4'bz;  // Controlled_Buffer controlled_buffer_10

  // Notes on the sheet:
  //   Feedback Path
  //   Data Bus
  //   Accumulator Register
  //   Memory Select Lines
endmodule

module Memory_Address_Generation (
  input  [3:0] in_1,
  input  Load_MAR,
  input  Use_PC,
  input  Clock,
  input  Reset
);

  wire [3:0] main_1_y0, main_2_y0, register_1_q, register_2_q;

  _4BIT_INC_main main_1 (
    .A3(register_1_q[3]), .A2(register_1_q[2]), .A1(register_1_q[1]), .A0(register_1_q[0]), .INC(1'b1),
    .Y3(main_1_y0[3]), .Y2(main_1_y0[2]), .Y1(main_1_y0[1]), .Y0(main_1_y0[0]));  // open: CRY
  Register #(.width(4)) register_1 (.D(main_1_y0), .en(Use_PC), .Q(register_1_q), .clk(Clock), .clr(Reset));
  Register #(.width(4)) register_2 (.D(in_1), .en(Load_MAR), .Q(register_2_q), .clk(Clock), .clr(Reset));
  Hex_Digit_Display hex_digit_display_1 (.value(register_1_q));  // open: dp
  Hex_Digit_Display hex_digit_display_2 (.value(register_2_q));  // open: dp
  Hex_Digit_Display hex_digit_display_3 (.value(main_2_y0));  // open: dp
  MUX_4_main main_2 (
    .A3(register_1_q[3]), .A2(register_1_q[2]), .A1(register_1_q[1]), .A0(register_1_q[0]),
    .B3(register_2_q[3]), .B2(register_2_q[2]), .B1(register_2_q[1]), .B0(register_2_q[0]), .A_nB(Use_PC),
    .Y3(main_2_y0[3]), .Y2(main_2_y0[2]), .Y1(main_2_y0[1]), .Y0(main_2_y0[0]));

  // Notes on the sheet:
  //   Program Counter Register
  //   Memory Address Register
endmodule

module Controller_Circuit (
  input  [3:0] in_1,
  input  Clock,
  input  Reset,
  output Not_Used,
  output Not_Used_2,
  output Not_Used_3,
  output Not_Used_4,
  output Logic_nArith,
  output nInvert,
  output nA_Only,
  output Use_PC,
  output Load_MAR,
  output Load_ACC,
  output ACC_to_Data_Bus,
  output Read,
  output Write,
  output Load_IR,
  output Next_State_Bit_1,
  output Next_State_Bit_0
);

  wire [1:0] register_2_q;
  wire [3:0] register_1_q;

  Register #(.width(4)) register_1 (.D(in_1), .en(Not_Used_3), .Q(register_1_q), .clk(Clock), .clr(Reset));
  Register #(.width(2)) register_2 (.D({Not_Used_2, Not_Used}), .en(1'b1), .Q(register_2_q), .clk(Clock), .clr(Reset));
  Hex_Digit_Display hex_digit_display_1 (.value(register_1_q));  // open: dp
  Hex_Digit_Display hex_digit_display_2 (.value({2'b00, register_2_q}));  // open: dp
  ROM #(.addrWidth(6), .dataWidth(16)) rom_1 (
    .addr({register_1_q, register_2_q}),
    .data({Next_State_Bit_0, Next_State_Bit_1, Load_IR, Write, Read, ACC_to_Data_Bus, Load_ACC, Load_MAR, Use_PC, nA_Only, nInvert, Logic_nArith, Not_Used_4, Not_Used_3, Not_Used_2, Not_Used}));  // open: sel

  // Notes on the sheet:
  //   contents of rom_1 (hex, n*v repeats v):
  //   115 550 0 0 115 750 0 0 115 1
endmodule

module MicroProcessor (
  input  [3:0] in_1,
  input  [3:0] in_2,
  input  [3:0] in_3,
  input  [3:0] in_4,
  input  [3:0] in_5,
  input  [3:0] in_6,
  input  [3:0] in_7,
  input  [3:0] in_8,
  input  Clock,
  input  Reset
);

  wire and_1_out, and_2_out, and_3_out, and_4_out, and_5_out, and_6_out, and_7_out, and_8_out, and_9_out,
       and_10_out, and_11_out, main_4_y14, main_4_y15;
  wire [1:0] register_2_q;
  wire [3:0] controlled_buffer_1_out, main_1_y0, main_2_y0, main_3_y0, register_1_q, register_3_q,
       register_4_q, register_5_q, register_6_q, register_7_q;
  wire [7:0] main_4_y0;
  wire [15:0] rom_1_data;

  Hex_Digit_Display hex_digit_display_1 (.value(rom_1_data[11:8]));  // open: dp
  Hex_Digit_Display hex_digit_display_2 (.value(rom_1_data[15:12]));  // open: dp
  Register #(.width(4)) register_1 (
    .D(controlled_buffer_1_out), .en(rom_1_data[2]), .Q(register_1_q), .clk(Clock), .clr(Reset));
  Register #(.width(2)) register_2 (.D(rom_1_data[1:0]), .en(1'b1), .Q(register_2_q), .clk(Clock), .clr(Reset));
  _4BIT_INC_main main_1 (
    .A3(register_3_q[3]), .A2(register_3_q[2]), .A1(register_3_q[1]), .A0(register_3_q[0]), .INC(1'b1),
    .Y3(main_1_y0[3]), .Y2(main_1_y0[2]), .Y1(main_1_y0[1]), .Y0(main_1_y0[0]));  // open: CRY
  Hex_Digit_Display hex_digit_display_3 (.value(rom_1_data[7:4]));  // open: dp
  Hex_Digit_Display hex_digit_display_4 (.value(rom_1_data[3:0]));  // open: dp
  Hex_Digit_Display hex_digit_display_5 (.value(register_1_q));  // open: dp
  Hex_Digit_Display hex_digit_display_6 (.value({2'b00, register_2_q}));  // open: dp
  Register #(.width(4)) register_3 (.D(main_1_y0), .en(rom_1_data[8]), .Q(register_3_q), .clk(Clock), .clr(Reset));
  Register #(.width(4)) register_4 (
    .D(controlled_buffer_1_out), .en(rom_1_data[7]), .Q(register_4_q), .clk(Clock), .clr(Reset));
  Hex_Digit_Display hex_digit_display_7 (.value(register_3_q));  // open: dp
  Hex_Digit_Display hex_digit_display_8 (.value(register_4_q));  // open: dp
  Hex_Digit_Display hex_digit_display_9 (.value(main_2_y0));  // open: dp
  ALU_main main_2 (
    .A3(controlled_buffer_1_out[3]), .A2(controlled_buffer_1_out[2]), .A1(controlled_buffer_1_out[1]),
    .A0(controlled_buffer_1_out[0]), .B3(register_5_q[3]), .B2(register_5_q[2]), .B1(register_5_q[1]),
    .B0(register_5_q[0]), .C_in(1'b0), .Logic__nArith(rom_1_data[11]), .nInvert(rom_1_data[10]),
    .nA_Only(rom_1_data[9]), .Y3(main_2_y0[3]), .Y2(main_2_y0[2]), .Y1(main_2_y0[1]), .Y0(main_2_y0[0]));  // open: C_Out
  Register #(.width(4)) register_5 (.D(main_2_y0), .en(rom_1_data[6]), .Q(register_5_q), .clk(Clock), .clr(Reset));
  ROM #(.addrWidth(6), .dataWidth(16)) rom_1 (.addr({register_1_q, register_2_q}), .data(rom_1_data));  // open: sel
  MUX_4_main main_3 (
    .A3(register_3_q[3]), .A2(register_3_q[2]), .A1(register_3_q[1]), .A0(register_3_q[0]),
    .B3(register_4_q[3]), .B2(register_4_q[2]), .B1(register_4_q[1]), .B0(register_4_q[0]),
    .A_nB(rom_1_data[8]), .Y3(main_3_y0[3]), .Y2(main_3_y0[2]), .Y1(main_3_y0[1]), .Y0(main_3_y0[0]));
  Hex_Digit_Display hex_digit_display_10 (.value(register_5_q));  // open: dp
  assign controlled_buffer_1_out = rom_1_data[5] ? register_5_q : 4'bz;  // Controlled_Buffer controlled_buffer_1
  Hex_Digit_Display hex_digit_display_11 (.value(main_3_y0));  // open: dp
  and and_1 (and_1_out, main_4_y14, rom_1_data[3]);
  and and_2 (and_2_out, main_4_y15, rom_1_data[3]);
  and and_3 (and_3_out, main_4_y15, rom_1_data[4]);
  Hex_Digit_Display hex_digit_display_12 (.value(register_6_q));  // open: dp
  Register #(.width(4)) register_6 (
    .D(controlled_buffer_1_out), .en(and_1_out), .Q(register_6_q), .clk(Clock), .clr(Reset));
  Register #(.width(4)) register_7 (
    .D(controlled_buffer_1_out), .en(and_2_out), .Q(register_7_q), .clk(Clock), .clr(Reset));
  DECODER4_16_main main_4 (
    .A0(main_3_y0[0]), .A1(main_3_y0[1]), .A2(main_3_y0[2]), .A3(main_3_y0[3]), .EN(1'b1), .Y0(main_4_y0[0]),
    .Y1(main_4_y0[1]), .Y2(main_4_y0[2]), .Y3(main_4_y0[3]), .Y4(main_4_y0[4]), .Y5(main_4_y0[5]),
    .Y6(main_4_y0[6]), .Y7(main_4_y0[7]), .Y14(main_4_y14), .Y15(main_4_y15));  // open: Y8, Y9, Y10, Y11, Y12, Y13
  assign controlled_buffer_1_out = and_3_out ? register_7_q : 4'bz;  // Controlled_Buffer controlled_buffer_2
  assign controlled_buffer_1_out = and_4_out ? in_1 : 4'bz;  // Controlled_Buffer controlled_buffer_3
  and and_4 (and_4_out, rom_1_data[4], main_4_y0[0]);
  assign controlled_buffer_1_out = and_5_out ? in_3 : 4'bz;  // Controlled_Buffer controlled_buffer_4
  and and_5 (and_5_out, rom_1_data[4], main_4_y0[1]);
  assign controlled_buffer_1_out = and_6_out ? in_5 : 4'bz;  // Controlled_Buffer controlled_buffer_5
  and and_6 (and_6_out, rom_1_data[4], main_4_y0[2]);
  assign controlled_buffer_1_out = and_7_out ? in_7 : 4'bz;  // Controlled_Buffer controlled_buffer_6
  and and_7 (and_7_out, rom_1_data[4], main_4_y0[3]);
  Hex_Digit_Display hex_digit_display_13 (.value(controlled_buffer_1_out));  // open: dp
  and and_8 (and_8_out, rom_1_data[4], main_4_y0[4]);
  and and_9 (and_9_out, rom_1_data[4], main_4_y0[5]);
  and and_10 (and_10_out, rom_1_data[4], main_4_y0[6]);
  and and_11 (and_11_out, rom_1_data[4], main_4_y0[7]);
  assign controlled_buffer_1_out = and_8_out ? in_2 : 4'bz;  // Controlled_Buffer controlled_buffer_7
  assign controlled_buffer_1_out = and_9_out ? in_4 : 4'bz;  // Controlled_Buffer controlled_buffer_8
  assign controlled_buffer_1_out = and_10_out ? in_6 : 4'bz;  // Controlled_Buffer controlled_buffer_9
  assign controlled_buffer_1_out = and_11_out ? in_8 : 4'bz;  // Controlled_Buffer controlled_buffer_10

  // Notes on the sheet:
  //   Program Counter Register
  //   Memory Address Register
  //   Feedback Path
  //   Data Bus
  //   Accumulator Register
  //   contents of rom_1 (hex, n*v repeats v):
  //   115 550 0 0 115 750 0 0 115 1 0 0 115 f50 0 0 115 26 1 2 115 350 0 0 115 192 28 0 115 494
  //   Address Bus
  //   Memory Select Lines
endmodule
